# Fritzing sketch MycoFarmV1 (saved by Fritzing 0.9.5d)
breadboards: 1

parts:
  Part1 = Arduino Uno (Rev3) - ICSP
  DHT1 = DHT11 Humitidy and Temperature Sensor
  Part2 = Adafruit CCS811
  U1 = 4RelayModule
  Raspberry_Pi_1 = Raspberry Pi 3 [part_number=RPI-3-V1.2]  # not connected

nets:
  N1: Part1.A4/SDA, Part2.SDA
  N2: Part1.A5/SCL, Part2.SCL
  N3: Part1.D8, DHT1.VDD
  N4: Part1.D10_PWM/SS, U1.IN4
  N5: Part1.D11_PWM/MOSI, U1.IN3
  N6: Part1.D12/MISO, U1.IN2
  N7: Part1.D13/SCK, U1.IN1
  5V: Part1.5V, DHT1.DATA, Part2.VIN, U1.VCC
  GND: Part1.GND, DHT1.NULL, Part2.GND, Part2.!WAKE, U1.GND

notes:
  Irrigation 24VAC
  Grow Lamp 5VDC
  FAE Fan 12VDC
  Pad Heater ??? DC
  Per Tub
  Master Controller
  DHT11/22 T&H Sensor
  CCS811 eCO2 Sensor

custom parts:
  DHT11 Humitidy and Temperature Sensor: DHT11 Humidity and Temperature Sensor
  4RelayModule: 4 relay arduino module SONGLE SRD05VDC-SL-C
